# Fritzing sketch Wrench-Mask-Wifi-ESP8266 (saved by Fritzing 0.9.3b)
breadboards: 1

parts:
  LPD8806_RGB_LED_Strip1 = LPD8806 RGB LED Strip
  U2 = 74AHCT125 [part_number=SN74AHCT125 package=dil14]
  Part1 = Adafruit Feather HUZZAH ESP8266 [part_number="Adafruit #2821"]
  LPD8806_RGB_LED_Strip2 = LPD8806 RGB LED Strip
  S1 = SPST Switch [package=switch-spdt]
  JACK1 = 2.1mm DC Barrel Jack

nets:
  N1: LPD8806_RGB_LED_Strip1.GND#0, U2.1OE, U2.2OE, U2.GND, U2.3A, U2.3OE, U2.4A, U2.4OE
  N2: LPD8806_RGB_LED_Strip1.DI, U2.1Y
  N3: LPD8806_RGB_LED_Strip1.CI, U2.2Y
  N4: LPD8806_RGB_LED_Strip1.+5V#3, U2.VCC
  N5: LPD8806_RGB_LED_Strip1.GND#4, LPD8806_RGB_LED_Strip2.GND, JACK1.sleeve
  N6: LPD8806_RGB_LED_Strip1.DO, LPD8806_RGB_LED_Strip2.DI
  N7: LPD8806_RGB_LED_Strip1.CO, LPD8806_RGB_LED_Strip2.CI
  N8: LPD8806_RGB_LED_Strip1.+5V#7, LPD8806_RGB_LED_Strip2.+5V, JACK1.center
  N9: U2.1A, Part1.GPIO13/MOSI
  N10: U2.2A, Part1.GPIO14/SCK
  N11: Part1.GND, S1.P
  N12: Part1.EN, S1.O

custom parts:
  LPD8806 RGB LED Strip: Digitally addressable RGB LED strip
  74AHCT125: Quad Level-Shifter (3V to 5V) Quadruple Bus Buffer Gates With 3-State Outputs
  Adafruit Feather HUZZAH ESP8266: his is the Adafruit Feather HUZZAH ESP8266 - our take on an 'all-in-one' ESP8266 WiFi development board with built in USB and battery charging. Its an ESP8266 WiFi module with all the extras you need, ready to rock! We have other boards in the Feather family, check'em out here. At the Feather HUZZAH's heart is an ESP8266 WiFi microcontroller clocked at 80 MHz and at 3.3V logic. This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
  2.1mm DC Barrel Jack: 2.1mm DC Barrel Jack with Thru-Hole Connectors (breadboardable)
