# Fritzing sketch Wrench-Mask-NRF24L01 (saved by Fritzing 0.9.3b)
breadboards: 1

parts:
  LPD8806_RGB_LED_Strip1 = LPD8806 RGB LED Strip
  U2 = 74AHCT125 [part_number=SN74AHCT125 package=dil14]
  LPD8806_RGB_LED_Strip2 = LPD8806 RGB LED Strip
  S1 = SPST Switch [package=switch-spdt]
  JACK1 = 2.1mm DC Barrel Jack
  NRF24L1 = NRF24L01
  Part3 = Adafruit Feather M0 Basic Proto [part_number="Adafruit #2772"]

nets:
  GND: LPD8806_RGB_LED_Strip1.GND#0, U2.1OE, U2.2OE, U2.GND, U2.3A, U2.3OE, U2.4A, U2.4OE, S1.O, NRF24L1.GND, Part3.GND
  N1: LPD8806_RGB_LED_Strip1.DI, U2.1Y
  N2: LPD8806_RGB_LED_Strip1.CI, U2.2Y
  N3: LPD8806_RGB_LED_Strip1.+5V#3, U2.VCC
  N4: LPD8806_RGB_LED_Strip1.GND#4, LPD8806_RGB_LED_Strip2.GND, JACK1.sleeve
  N5: LPD8806_RGB_LED_Strip1.DO, LPD8806_RGB_LED_Strip2.DI
  N6: LPD8806_RGB_LED_Strip1.CO, LPD8806_RGB_LED_Strip2.CI
  N7: LPD8806_RGB_LED_Strip1.+5V#7, LPD8806_RGB_LED_Strip2.+5V, JACK1.center
  N8: U2.1A, Part3.D6
  N9: U2.2A, Part3.D5
  N10: S1.P, Part3.EN
  VCC: NRF24L1.VCC, Part3.+3V3
  N11: NRF24L1.CSN, Part3.D10
  N12: NRF24L1.MOSI, Part3.MOSI
  N13: NRF24L1.CE, Part3.D11
  N14: NRF24L1.SCK, Part3.SCK
  N15: NRF24L1.MISO, Part3.MISO

custom parts:
  LPD8806 RGB LED Strip: Digitally addressable RGB LED strip
  74AHCT125: Quad Level-Shifter (3V to 5V) Quadruple Bus Buffer Gates With 3-State Outputs
  2.1mm DC Barrel Jack: 2.1mm DC Barrel Jack with Thru-Hole Connectors (breadboardable)
  NRF24L01: NRF24L01 module
  Adafruit Feather M0 Basic Proto: At the Feather M0's heart is an ATSAMD21G18 ARM Cortex M0 processor, clocked at 48 MHz and at 3.3V logic, the same one used in the new Arduino Zero. This chip has a whopping 256K of FLASH (8x more than the Atmega328 or 32u4) and 32K of RAM (16x as much)! This chip comes with built in USB so it has USB-to-Serial program & debug capability built in with no need for an FTDI-like chip. To make it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
